# Fritzing sketch final_project (saved by Fritzing 0.9.10b)
breadboards: 1

parts:
  J1 = STM32 Nucleo boards
  Part1 = Adafruit Si7021 Humidity and Temperature Sensor [part_number="Adafruit #3251"]
  Part2 = Adafruit Ultimate GPS v3 [part_number="Adafruit #746"]  # not connected
  Part3 = Adafruit MMA8451 Accelerometer [part_number="Adafruit #2019"]
  Q1 = LTR-301 [package=ltr-301]  # not connected
  Part4 = Adafruit TCS34725 RGB Color Sensor [part_number="Adafruit #1334"]
  Part5 = Soil Moisture Sensor  # not connected

nets:
  N1: J1.A4/SDA#114, Part4.SDA
  N2: J1.A5/SCL#115, Part4.SCL
  N3: J1.A4/SDA#1159, Part1.SDA, Part3.SDA
  N4: J1.A5/SCL#1160, Part1.SCL, Part3.SCL
  VIN: J1.3V3, Part1.VCC, Part3.VIN, Part4.VIN
  GND: J1.GND, Part1.GND, Part3.GND, Part4.GND

custom parts:
  Adafruit Si7021 Humidity and Temperature Sensor: It's summer and you're sweating and your hair's all frizzy and all you really want to know is why the weatherman said this morning that today's relative humidity would max out at a perfectly reasonable 42% when it feels more like 77%. Enter the Si7021 Temperature + Humidity Sensor - the best way to prove the weatherman wrong! This lovely sensor for Silicon labs has ± 3% relative humidity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
  Adafruit Ultimate GPS v3: We carry a few different GPS modules here in the Adafruit shop, but none that satisfied our every desire - that's why we designed this little GPS breakout board. We believe this is the Ultimate GPS module, so we named it that. It's got everything you want and more: -165 dBm sensitivity, 10 Hz updates, 66 channels 5V friendly design and only 20mA current draw Breadboard friendly + two mounting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
  Adafruit MMA8451 Accelerometer: So many accelerometers and so little time! We've expanded our accelerometer selection even more with this high-precision and inexpensive MMA8451 Triple-Axis Accelerometer w/ 14-bit ADC. You can detect motion, tilt and basic orientation with a digital accelerometer - and the MMA8451 is a great accelerometer to start with. It has a wide usage range, from +-2g up to +-8g yet is easy to use with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
  Adafruit TCS34725 RGB Color Sensor: Your electronics can now see in dazzling color with this lovely color light sensor. We found the best color sensor on the market, the TCS34725, which has RGB and Clear light sensing elements. An IR blocking filter, integrated on-chip and localized to the color sensing photodiodes, minimizes the IR spectral component of the incoming light and allows color measurements to be made accurately. The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
